# Fritzing sketch SmartCoil_sketch (saved by Fritzing 0.9.3b)

parts:
  proto1 = Adafruit_PermaProto_1_4_Board
  Raspberry_Pi_1 = Raspberry Pi 3 [part_number=RPI-3-V1.2]
  Part1 = Adafruit BME680  # not connected
  U1 = 4-Channel 5v Relay Shield [package=relay-4ch5v10a]  # not connected

nets:
  N1: proto1.connectorE1, Raspberry_Pi_1.GPIO2
  3V3: proto1.connectorW1, proto1.connectorZ1, Raspberry_Pi_1.3v3, Raspberry_Pi_1.3V3
  N2: proto1.connectorX1, Raspberry_Pi_1.GND
  N3: proto1.connectorY1, Raspberry_Pi_1.5V

custom parts:
  4-Channel 5v Relay Shield: 4 Channel 5v Relay Shield w. 2x SPD-06VDC-SD-C
